// Logisim project 作业12 2019 Project-第2次提交.circ as structural Verilog: 1 circuit, main circuit Add Circuit
module Add_Circuit (
  input  zero,
  output [7:0] out,
  output [7:0] out_3
);

  wire clock_1_out;

  Adder adder_1 (.a(8'h1), .b(out_3), .out(out));  // open: cin, cout
  Register register_1 (.D(out), .Q(out_3), .clk(clock_1_out), .clr(zero));  // open: en
  Clock clock_1 (.out(clock_1_out));
endmodule
