// Logisim project 作业8 2019Project-第1次提交-加法器 .circ as structural Verilog: 5 circuits, main circuit FA
module FA (
  input  X,
  input  Y,
  input  C0,
  output F,
  output Ci
);

  wire and_1_out, and_2_out, and_3_out, xor_1_out;

  xor xor_1 (xor_1_out, X, Y);
  and and_1 (and_1_out, X, Y);
  and and_2 (and_2_out, C0, X);
  and and_3 (and_3_out, Y, C0);
  or or_1 (Ci, and_1_out, and_2_out, and_3_out);
  xor xor_2 (F, xor_1_out, C0);
endmodule

module A_S (
  input  Y,
  input  Sub,
  input  X,
  input  C0,
  output Ci,
  output F
);

  wire xor_1_out;

  xor xor_1 (xor_1_out, Y, Sub);
  FA fa_1 (.X(X), .Y(xor_1_out), .C0(C0), .Ci(Ci), .F(F));
endmodule

module _8bit_adder (
  input  [7:0] X,
  input  [7:0] Y,
  input  SUB,
  output [7:0] X_2,
  output C
);

  wire a_s_2_ci, a_s_3_ci, a_s_4_ci, a_s_5_ci, a_s_6_ci, a_s_7_ci, a_s_8_ci;

  A_S a_s_1 (.Y(Y[7]), .Sub(SUB), .X(X[7]), .C0(a_s_2_ci), .Ci(C), .F(X_2[7]));
  A_S a_s_2 (.Y(Y[6]), .Sub(SUB), .X(X[6]), .C0(a_s_3_ci), .Ci(a_s_2_ci), .F(X_2[6]));
  A_S a_s_3 (.Y(Y[5]), .Sub(SUB), .X(X[5]), .C0(a_s_4_ci), .Ci(a_s_3_ci), .F(X_2[5]));
  A_S a_s_4 (.Y(Y[4]), .Sub(SUB), .X(X[4]), .C0(a_s_5_ci), .Ci(a_s_4_ci), .F(X_2[4]));
  A_S a_s_5 (.Y(Y[3]), .Sub(SUB), .X(X[3]), .C0(a_s_6_ci), .Ci(a_s_5_ci), .F(X_2[3]));
  A_S a_s_6 (.Y(Y[2]), .Sub(SUB), .X(X[2]), .C0(a_s_7_ci), .Ci(a_s_6_ci), .F(X_2[2]));
  A_S a_s_7 (.Y(Y[1]), .Sub(SUB), .X(X[1]), .C0(a_s_8_ci), .Ci(a_s_7_ci), .F(X_2[1]));
  A_S a_s_8 (.Y(Y[0]), .Sub(SUB), .X(X[0]), .C0(SUB), .Ci(a_s_8_ci), .F(X_2[0]));
endmodule

module _4bit_adder (
  input  [3:0] X,
  input  [3:0] Y,
  input  SUB,
  input  C_in,
  output [3:0] F,
  output C
);

  wire a_s_2_ci, a_s_3_ci, a_s_4_ci;

  A_S a_s_1 (.Y(Y[3]), .Sub(SUB), .X(X[3]), .C0(a_s_2_ci), .Ci(C), .F(F[3]));
  A_S a_s_2 (.Y(Y[2]), .Sub(SUB), .X(X[2]), .C0(a_s_3_ci), .Ci(a_s_2_ci), .F(F[2]));
  A_S a_s_3 (.Y(Y[1]), .Sub(SUB), .X(X[1]), .C0(a_s_4_ci), .Ci(a_s_3_ci), .F(F[1]));
  A_S a_s_4 (.Y(Y[0]), .Sub(SUB), .X(X[0]), .C0(C_in), .Ci(a_s_4_ci), .F(F[0]));
endmodule

module _8bit_adder2 (
  input  Sub,
  input  [7:0] X,
  input  [7:0] Y,
  output [7:0] out_4,
  output C
);

  wire n4bit_adder_2_c;

  _4bit_adder u_4bit_adder_1 (.F(out_4[7:4]), .X(X[7:4]), .Y(Y[7:4]), .SUB(Sub), .C(C), .C_in(n4bit_adder_2_c));
  _4bit_adder u_4bit_adder_2 (.F(out_4[3:0]), .X(X[3:0]), .Y(Y[3:0]), .SUB(Sub), .C(n4bit_adder_2_c), .C_in(Sub));
endmodule
