// Logisim project 第一题.circ as structural Verilog: 5 circuits, main circuit main
module main (
  input  X,
  input  Y,
  input  C0,
  output F,
  output Ci
);

  wire and_1_out, and_2_out, and_3_out, xor_1_out;

  xor xor_1 (xor_1_out, X, Y);
  and and_1 (and_1_out, X, Y);
  and and_2 (and_2_out, C0, X);
  and and_3 (and_3_out, Y, C0);
  xor xor_2 (F, xor_1_out, C0);
  or or_1 (Ci, and_1_out, and_2_out, and_3_out);
endmodule

module FA (
  input  X,
  input  Y,
  input  C0,
  output F,
  output Ci
);

  wire and_1_out, and_2_out, and_3_out, xor_1_out;

  xor xor_1 (xor_1_out, X, Y);
  and and_1 (and_1_out, X, Y);
  and and_2 (and_2_out, C0, X);
  and and_3 (and_3_out, Y, C0);
  or or_1 (Ci, and_1_out, and_2_out, and_3_out);
  xor xor_2 (F, xor_1_out, C0);
endmodule

module A_S (
  input  Y,
  input  Sub,
  input  X,
  input  C0,
  output Ci,
  output F
);

  wire xor_1_out;

  xor xor_1 (xor_1_out, Y, Sub);
  FA fa_1 (.X(X), .Y(xor_1_out), .C0(C0), .Ci(Ci), .F(F));
endmodule

module _4bit (
  input  Start,
  input  Clear,
  input  SUB,
  output [3:0] X,
  output C,
  output [3:0] X_2,
  output [3:0] Y
);

  wire a_s_2_ci, a_s_3_ci, a_s_4_ci, X_out, Y_out;

  Clock u_X (.out(X_out));
  Clock u_Y (.out(Y_out));
  Counter #(.width(4), .max('hf)) counter_1 (.count(Start), .Q(X_2), .clk(X_out), .clr(Clear));  // open: load, D, carry
  Counter #(.width(4), .max('hf)) counter_2 (.count(Start), .Q(Y), .clk(Y_out), .clr(Clear));  // open: load, D, carry
  A_S a_s_1 (.Y(Y[3]), .Sub(SUB), .X(X_2[3]), .C0(a_s_2_ci), .Ci(C), .F(X[3]));
  A_S a_s_2 (.Y(Y[2]), .Sub(SUB), .X(X_2[2]), .C0(a_s_3_ci), .Ci(a_s_2_ci), .F(X[2]));
  A_S a_s_3 (.Y(Y[1]), .Sub(SUB), .X(X_2[1]), .C0(a_s_4_ci), .Ci(a_s_3_ci), .F(X[1]));
  A_S a_s_4 (.Y(Y[0]), .Sub(SUB), .X(X_2[0]), .C0(SUB), .Ci(a_s_4_ci), .F(X[0]));
  LED led_1 (.in(X[0]));
  LED led_2 (.in(X[1]));
  LED led_3 (.in(X[2]));
  LED led_4 (.in(X[3]));
endmodule

module _4bit1 (
  input  [3:0] X,
  input  [3:0] Y,
  input  SUB,
  output [3:0] X_2,
  output C
);

  wire a_s_2_ci, a_s_3_ci, a_s_4_ci;

  A_S a_s_1 (.Y(Y[3]), .Sub(SUB), .X(X[3]), .C0(a_s_2_ci), .Ci(C), .F(X_2[3]));
  A_S a_s_2 (.Y(Y[2]), .Sub(SUB), .X(X[2]), .C0(a_s_3_ci), .Ci(a_s_2_ci), .F(X_2[2]));
  A_S a_s_3 (.Y(Y[1]), .Sub(SUB), .X(X[1]), .C0(a_s_4_ci), .Ci(a_s_3_ci), .F(X_2[1]));
  A_S a_s_4 (.Y(Y[0]), .Sub(SUB), .X(X[0]), .C0(SUB), .Ci(a_s_4_ci), .F(X_2[0]));
endmodule
